// Logisim project AsteroidPong.circ as structural Verilog: 5 circuits, main circuit main
module main (
  input  in_1,
  input  in_2,
  output out_3
);

  wire clock_1_out;
  wire [6:0] keyboard_1_data;
  wire [31:0] player_1_out_2;

  Clock clock_1 (.out(clock_1_out));
  Keyboard keyboard_1 (.clk(clock_1_out), .re(in_1), .clr(in_2), .avail(out_3), .data(keyboard_1_data));
  Player player_1 (.in_1(keyboard_1_data), .out_2(player_1_out_2));
  DotMatrix #(.inputtype("row"), .matrixcols(32), .matrixrows(32)) dotmatrix_1 (.row31(player_1_out_2));  // open: row0, row1, row2, row3, row4, row5, row6, row7, row8, row9, row10, row11, row12, row13, row14, row15, row16, row17, row18, row19, row20, row21, row22, row23, row24, row25, row26, row27, row28, row29, row30
endmodule

module Player (
  input  [6:0] in_1,
  output [31:0] out_2
);

  wire comparator_1_eq, comparator_2_eq, playermovselect_1_anterior, playermovselect_1_siguiente;
  wire [4:0] counter_1_q;

  Comparator #(.width(7), .mode("unsigned")) comparator_1 (
    .a(7'b1100001), .b(in_1), .eq(comparator_1_eq));  // open: gt, lt
  Comparator #(.width(7), .mode("unsigned")) comparator_2 (
    .a(7'b1100100), .b(in_1), .eq(comparator_2_eq));  // open: gt, lt
  PlayerMovSelect playermovselect_1 (
    .a(comparator_1_eq), .d(comparator_2_eq), .anterior(playermovselect_1_anterior),
    .siguiente(playermovselect_1_siguiente));
  PlayerMovement playermovement_1 (.in_1(counter_1_q), .out_2(out_2));
  Counter #(.width(5), .max('h1f)) counter_1 (
    .load(playermovselect_1_anterior), .Q(counter_1_q), .clk(playermovselect_1_siguiente));  // open: D, count, carry, clr
endmodule

module PlayerMovSelect (
  input  a,
  input  d,
  output anterior,
  output siguiente
);

  wire and_2_out, and_3_out, not_1_out, not_2_out, not_3_out;

  not not_1 (not_1_out, d);
  not not_2 (not_2_out, a);
  not not_3 (not_3_out, d);
  and and_1 (anterior, a, not_1_out);
  and and_2 (and_2_out, not_2_out, d);
  and and_3 (and_3_out, a, not_3_out);
  or or_1 (siguiente, and_2_out, and_3_out);
endmodule

module RandomSystem (
  input  in_1,
  input  in_2,
  input  in_3,
  input  in_4
);

  wire [2:0] random_1_out, random_2_out, random_3_out;
  wire [7:0] decoder_1_out7, decoder_2_out7, decoder_3_out7;
  wire [9:0] bit_extender_3_out;
  wire [10:0] bit_extender_1_out, bit_extender_2_out;

  Random #(.width(3)) random_1 (.clk(in_4), .next(in_1), .out(random_1_out));  // open: clr
  Random #(.width(3)) random_2 (.clk(in_4), .next(in_2), .out(random_2_out));  // open: clr
  Random #(.width(3)) random_3 (.clk(in_4), .next(in_3), .out(random_3_out));  // open: clr
  Decoder #(.select(3)) decoder_1 (
    .out0(decoder_1_out7[7]), .out1(decoder_1_out7[6]), .out2(decoder_1_out7[5]), .out3(decoder_1_out7[4]),
    .out4(decoder_1_out7[3]), .out5(decoder_1_out7[2]), .out6(decoder_1_out7[1]), .out7(decoder_1_out7[0]),
    .sel(random_1_out));  // open: en
  Decoder #(.select(3)) decoder_2 (
    .out0(decoder_2_out7[7]), .out1(decoder_2_out7[6]), .out2(decoder_2_out7[5]), .out3(decoder_2_out7[4]),
    .out4(decoder_2_out7[3]), .out5(decoder_2_out7[2]), .out6(decoder_2_out7[1]), .out7(decoder_2_out7[0]),
    .sel(random_2_out));  // open: en
  Decoder #(.select(3)) decoder_3 (
    .out0(decoder_3_out7[7]), .out1(decoder_3_out7[6]), .out2(decoder_3_out7[5]), .out3(decoder_3_out7[4]),
    .out4(decoder_3_out7[3]), .out5(decoder_3_out7[2]), .out6(decoder_3_out7[1]), .out7(decoder_3_out7[0]),
    .sel(random_3_out));  // open: en
  assign bit_extender_1_out = {{3{1'b0}}, decoder_1_out7};  // Bit_Extender bit_extender_1
  assign bit_extender_2_out = {{3{1'b0}}, decoder_3_out7};  // Bit_Extender bit_extender_2
  assign bit_extender_3_out = {{2{1'b0}}, decoder_2_out7};  // Bit_Extender bit_extender_3
  DotMatrix #(.inputtype("row"), .matrixcols(32), .matrixrows(32)) dotmatrix_1 (.row0({bit_extender_3_out, bit_extender_2_out, bit_extender_1_out}));  // open: row1, row2, row3, row4, row5, row6, row7, row8, row9, row10, row11, row12, row13, row14, row15, row16, row17, row18, row19, row20, row21, row22, row23, row24, row25, row26, row27, row28, row29, row30, row31
endmodule

module PlayerMovement (
  input  [4:0] in_1,
  output [31:0] out_2
);

  Multiplexer #(.select(5), .width(32)) multiplexer_1 (
    .in0(32'he0000000), .in1(32'h70000000), .in2(32'h38000000), .in3(32'h1c000000), .in4(32'he000000),
    .in5(32'h7000000), .in6(32'h3800000), .in7(32'h1c00000), .in8(32'he00000), .in9(32'h700000),
    .in10(32'h380000), .in11(32'h1c0000), .in12(32'he0000), .in13(32'h70000), .in14(32'h38000),
    .in15(32'h1c000), .in16(32'he000), .in17(32'h7000), .in18(32'h3800), .in19(32'h1c00), .in20(32'he00),
    .in21(32'h700), .in22(32'h380), .in23(32'h1c0), .in24(32'he0), .in25(32'h70), .in26(32'h38),
    .in27(32'h1c), .in28(32'he), .in29(32'h7), .in30(32'h80000003), .in31(32'hc0000001), .out(out_2),
    .sel(in_1));  // open: en
endmodule
